# Fritzing sketch schematic (saved by Fritzing 0.9.0b)
breadboards: 1

parts:
  R1 = Resistor [tolerance=±5% resistance=270 package=THT]
  LED1 = RGB LED (com. cathode, rgb) [package="5 mm [THT]"]
  Part1 = Spark Core (v1.0)
  R2 = Resistor [tolerance=±5% resistance=270 package=THT]
  R3 = Resistor [tolerance=±5% resistance=270 package=THT]

nets:
  N1: R1.Pin_0, LED1.red_anode
  N2: R1.Pin_1, Part1.D2
  N3: LED1.common_cathode, Part1.3V3*
  N4: LED1.green_anode, R2.Pin_0
  N5: LED1.blue_anode, R3.Pin_0
  N6: Part1.D0, R3.Pin_1
  N7: Part1.D1, R2.Pin_1
